// Logisim project smips.circ as structural Verilog: 9 circuits, main circuit Board
module Board (
);

  wire CLK, HALT, MEM_WE, RESET, TTY_WE;
  wire [3:0] MEM_BE;
  wire [6:0] TTY_DATA;
  wire [31:0] MEM_ADDR, MEM_RDATA, MEM_WDATA;

  Clock Reloj (.out(CLK));
  Button u_Reset (.out(RESET));
  CPU cpu_1 (
    .CLK(CLK), .RESET(RESET), .MEM_RDATA(MEM_RDATA), .MEM_ADDR(MEM_ADDR), .MEM_WDATA(MEM_WDATA),
    .MEM_BE(MEM_BE), .MEM_WE(MEM_WE), .TTY_DATA(TTY_DATA), .TTY_WE(TTY_WE), .HALT(HALT));
  TTY #(.cols(48), .rows(12)) tty_1 (.data(TTY_DATA), .clk(CLK), .we(TTY_WE), .clr(RESET));
  Memory memory_1 (.CLK(CLK), .ADDR(MEM_ADDR), .WDATA(MEM_WDATA), .BE(MEM_BE), .WE(MEM_WE), .RDATA(MEM_RDATA));
  LED u_Halt (.in(HALT));

  // Notes on the sheet:
  //   S-MIPS | Board
  //   No modificar: la CPU se implementa dentro del subcircuito CPU.
endmodule

module CPU (
  input  CLK,
  input  RESET,
  input  [31:0] MEM_RDATA,
  output [31:0] MEM_ADDR,
  output [31:0] MEM_WDATA,
  output [3:0] MEM_BE,
  output MEM_WE,
  output [6:0] TTY_DATA,
  output TTY_WE,
  output HALT
);

  Control_Unit control_unit_1 ();  // open: IRWRITE, ADDRSEL, PCSRC, PCWRITE, BRANCH, ALUSRCA, ALUSRCB, ALUOP, REGWRITE, REGDST, WDSEL, SYSSEL, MEM_WE, TTY_WE, HALT
  Instruction_Decoder instruction_decoder_1 ();  // open: OP, FUNCT, CLASS, ALUOP, EXTZERO, BNE, BYTE, UNSIGNED
  Branch_Control branch_control_1 ();  // open: PC_EN
  Datapath datapath_1 ();  // open: MEM_ADDR, MEM_WDATA, MEM_BE, OP, FUNCT, ZERO, V0_IS_10, V0_IS_11, TTY_DATA

  // Notes on the sheet:
  //   CPU S-MIPS: implementar aqui
  //   No cambiar nombres, anchos ni sentido de los pines: la placa depende de ellos.
endmodule

module Memory (
  input  CLK,
  input  [31:0] ADDR,
  input  [31:0] WDATA,
  input  [3:0] BE,
  input  WE,
  output [31:0] RDATA
);

  RAM #(.addrWidth(12), .asyncread("true"), .byteenables("byteEnables"), .dataWidth(32), .\type ("nonvolatile")) Main_Memory (
    .addr(ADDR[13:2]), .we(WE), .oe(1'b1), .clk(CLK), .din(WDATA), .dout(RDATA), .be3(BE[3]), .be2(BE[2]),
    .be1(BE[1]), .be0(BE[0]));

  // Other names for the same wires on the sheet: A[11:0] = ADDR[13:2]

  // Notes on the sheet:
  //   Memoria unificada: 4096 palabras de 32 bits (16 KiB), little-endian
  //   Lectura combinacional; escritura en el flanco de subida de CLK con WE=1, solo en los bytes con BE=1.
  //   Se usan los bits 13..2 de ADDR; los demas se ignoran (el espacio se repite cada 16 KiB).
endmodule

module Instruction_Decoder (
  input  [5:0] OP,
  input  [5:0] FUNCT,
  output [3:0] CLASS,
  output [2:0] ALUOP,
  output EXTZERO,
  output BNE,
  output BYTE,
  output UNSIGNED
);
endmodule

module Control_Unit (
  output IRWRITE,
  output ADDRSEL,
  output [1:0] PCSRC,
  output PCWRITE,
  output BRANCH,
  output [1:0] ALUSRCA,
  output [2:0] ALUSRCB,
  output [2:0] ALUOP,
  output REGWRITE,
  output [1:0] REGDST,
  output [1:0] WDSEL,
  output SYSSEL,
  output MEM_WE,
  output TTY_WE,
  output HALT
);
endmodule

module Branch_Control (
  output PC_EN
);
endmodule

module Datapath (
  output [31:0] MEM_ADDR,
  output [31:0] MEM_WDATA,
  output [3:0] MEM_BE,
  output [5:0] OP,
  output [5:0] FUNCT,
  output ZERO,
  output V0_IS_10,
  output V0_IS_11,
  output [6:0] TTY_DATA
);

  Register_File register_file_1 ();  // open: CLK, RESET, WE, RA1, RA2, WA, WD, RD1, RD2
  ALU alu_1 ();  // open: A, B, OP, RESULT, ZERO
endmodule

module Register_File (
  input  CLK,
  input  RESET,
  input  WE,
  input  [4:0] RA1,
  input  [4:0] RA2,
  input  [4:0] WA,
  input  [31:0] WD,
  output [31:0] RD1,
  output [31:0] RD2
);

  wire EN_1, EN_2, EN_3, EN_4, EN_5, EN_6, EN_7, EN_8, EN_9, EN_10, EN_11, EN_12, EN_13, EN_14, EN_15, EN_16,
       EN_17, EN_18, EN_19, EN_20, EN_21, EN_22, EN_23, EN_24, EN_25, EN_26, EN_27, EN_28, EN_29, EN_30,
       EN_31;
  wire [31:0] R_1, R_2, R_3, R_4, R_5, R_6, R_7, R_8, R_9, R_10, R_11, R_12, R_13, R_14, R_15, R_16, R_17,
       R_18, R_19, R_20, R_21, R_22, R_23, R_24, R_25, R_26, R_27, R_28, R_29, R_30, R_31, S_28, S_29, WD_28,
       WD_29;

  assign WD_28 = WD ^ 32'h1800;  // XOR_Gate xor_1, 32 bits wide
  assign WD_29 = WD ^ 32'h3ffc;  // XOR_Gate xor_2, 32 bits wide
  assign R_28 = S_28 ^ 32'h1800;  // XOR_Gate xor_3, 32 bits wide
  assign R_29 = S_29 ^ 32'h3ffc;  // XOR_Gate xor_4, 32 bits wide
  Decoder #(.select(5)) decoder_1 (
    .out1(EN_1), .out2(EN_2), .out3(EN_3), .out4(EN_4), .out5(EN_5), .out6(EN_6), .out7(EN_7), .out8(EN_8),
    .out9(EN_9), .out10(EN_10), .out11(EN_11), .out12(EN_12), .out13(EN_13), .out14(EN_14), .out15(EN_15),
    .out16(EN_16), .out17(EN_17), .out18(EN_18), .out19(EN_19), .out20(EN_20), .out21(EN_21), .out22(EN_22),
    .out23(EN_23), .out24(EN_24), .out25(EN_25), .out26(EN_26), .out27(EN_27), .out28(EN_28), .out29(EN_29),
    .out30(EN_30), .out31(EN_31), .sel(WA), .en(WE));  // open: out0
  Register #(.width(32)) R1 (.D(WD), .en(EN_1), .clk(CLK), .Q(R_1), .clr(RESET));
  Register #(.width(32)) R2 (.D(WD), .en(EN_2), .clk(CLK), .Q(R_2), .clr(RESET));
  Register #(.width(32)) R3 (.D(WD), .en(EN_3), .clk(CLK), .Q(R_3), .clr(RESET));
  Register #(.width(32)) R4 (.D(WD), .en(EN_4), .clk(CLK), .Q(R_4), .clr(RESET));
  Register #(.width(32)) R5 (.D(WD), .en(EN_5), .clk(CLK), .Q(R_5), .clr(RESET));
  Register #(.width(32)) R6 (.D(WD), .en(EN_6), .clk(CLK), .Q(R_6), .clr(RESET));
  Register #(.width(32)) R7 (.D(WD), .en(EN_7), .clk(CLK), .Q(R_7), .clr(RESET));
  Register #(.width(32)) R8 (.D(WD), .en(EN_8), .clk(CLK), .Q(R_8), .clr(RESET));
  Register #(.width(32)) R9 (.D(WD), .en(EN_9), .clk(CLK), .Q(R_9), .clr(RESET));
  Register #(.width(32)) R10 (.D(WD), .en(EN_10), .clk(CLK), .Q(R_10), .clr(RESET));
  Register #(.width(32)) R11 (.D(WD), .en(EN_11), .clk(CLK), .Q(R_11), .clr(RESET));
  Register #(.width(32)) R12 (.D(WD), .en(EN_12), .clk(CLK), .Q(R_12), .clr(RESET));
  Register #(.width(32)) R13 (.D(WD), .en(EN_13), .clk(CLK), .Q(R_13), .clr(RESET));
  Register #(.width(32)) R14 (.D(WD), .en(EN_14), .clk(CLK), .Q(R_14), .clr(RESET));
  Register #(.width(32)) R15 (.D(WD), .en(EN_15), .clk(CLK), .Q(R_15), .clr(RESET));
  Register #(.width(32)) R16 (.D(WD), .en(EN_16), .clk(CLK), .Q(R_16), .clr(RESET));
  Register #(.width(32)) R17 (.D(WD), .en(EN_17), .clk(CLK), .Q(R_17), .clr(RESET));
  Register #(.width(32)) R18 (.D(WD), .en(EN_18), .clk(CLK), .Q(R_18), .clr(RESET));
  Register #(.width(32)) R19 (.D(WD), .en(EN_19), .clk(CLK), .Q(R_19), .clr(RESET));
  Register #(.width(32)) R20 (.D(WD), .en(EN_20), .clk(CLK), .Q(R_20), .clr(RESET));
  Register #(.width(32)) R21 (.D(WD), .en(EN_21), .clk(CLK), .Q(R_21), .clr(RESET));
  Register #(.width(32)) R22 (.D(WD), .en(EN_22), .clk(CLK), .Q(R_22), .clr(RESET));
  Register #(.width(32)) R23 (.D(WD), .en(EN_23), .clk(CLK), .Q(R_23), .clr(RESET));
  Register #(.width(32)) R24 (.D(WD), .en(EN_24), .clk(CLK), .Q(R_24), .clr(RESET));
  Register #(.width(32)) R25 (.D(WD), .en(EN_25), .clk(CLK), .Q(R_25), .clr(RESET));
  Register #(.width(32)) R26 (.D(WD), .en(EN_26), .clk(CLK), .Q(R_26), .clr(RESET));
  Register #(.width(32)) R27 (.D(WD), .en(EN_27), .clk(CLK), .Q(R_27), .clr(RESET));
  Register #(.width(32)) R28 (.D(WD_28), .en(EN_28), .clk(CLK), .Q(S_28), .clr(RESET));
  Register #(.width(32)) R29 (.D(WD_29), .en(EN_29), .clk(CLK), .Q(S_29), .clr(RESET));
  Register #(.width(32)) R30 (.D(WD), .en(EN_30), .clk(CLK), .Q(R_30), .clr(RESET));
  Register #(.width(32)) R31 (.D(WD), .en(EN_31), .clk(CLK), .Q(R_31), .clr(RESET));
  Multiplexer #(.select(5), .width(32)) multiplexer_1 (
    .in0({32{1'b0}}), .in1(R_1), .in2(R_2), .in3(R_3), .in4(R_4), .in5(R_5), .in6(R_6), .in7(R_7), .in8(R_8),
    .in9(R_9), .in10(R_10), .in11(R_11), .in12(R_12), .in13(R_13), .in14(R_14), .in15(R_15), .in16(R_16),
    .in17(R_17), .in18(R_18), .in19(R_19), .in20(R_20), .in21(R_21), .in22(R_22), .in23(R_23), .in24(R_24),
    .in25(R_25), .in26(R_26), .in27(R_27), .in28(R_28), .in29(R_29), .in30(R_30), .in31(R_31), .out(RD1),
    .sel(RA1));
  Multiplexer #(.select(5), .width(32)) multiplexer_2 (
    .in0({32{1'b0}}), .in1(R_1), .in2(R_2), .in3(R_3), .in4(R_4), .in5(R_5), .in6(R_6), .in7(R_7), .in8(R_8),
    .in9(R_9), .in10(R_10), .in11(R_11), .in12(R_12), .in13(R_13), .in14(R_14), .in15(R_15), .in16(R_16),
    .in17(R_17), .in18(R_18), .in19(R_19), .in20(R_20), .in21(R_21), .in22(R_22), .in23(R_23), .in24(R_24),
    .in25(R_25), .in26(R_26), .in27(R_27), .in28(R_28), .in29(R_29), .in30(R_30), .in31(R_31), .out(RD2),
    .sel(RA2));

  // Notes on the sheet:
  //   Recibe el numero WA y activa
  //   SOLO la salida EN_n de ese
  //   registro, y solo si WE = 1.
  //   Cada EN_n habilita a un
  //   registro. La salida EN_0 no
  //   se conecta: asi $0 no se
  //   puede escribir nunca.
  //   CLK: reloj (se escribe al subir)
  //   RESET: 1 = vuelve al estado inicial
  //   WE: 1 = permite escribir ahora
  //   RA1: registro a leer (0-31) en RD1
  //   RA2: registro a leer (0-31) en RD2
  //   WA: registro donde se escribe (0-31)
  //   WD: dato de 32 bits que se escribe
  //   Decodificador de escritura (WA + WE)
  //   $gp y $sp: se guardan en XOR con su valor inicial; asi RESET (a 0) los deja en 0x1800 y 0x3FFC
  //   ESCRIBIR $gp: guarda WD XOR 0x1800
  //   ESCRIBIR $sp: guarda WD XOR 0x3FFC
  //   LEER $gp: valor guardado XOR 0x1800
  //   LEER $sp: valor guardado XOR 0x3FFC
  //   $zero: constante 0, siempre vale 0
  //   Register_File: 32 registros de 32 bits, 2 lecturas combinacionales, 1 escritura en flanco de subida
  //   $zero (R_0) = constante 0 y no se escribe nunca. RESET=1 pone los registros a 0 (asincrono).
  //   Registros $1 a $31 (cada uno: D=WD, EN=EN_n, CK=CLK, CLR=RESET)
  //   COMO LEER ESTE CIRCUITO (de izquierda a derecha)
  //   1. ENTRADAS: cada pin de la izquierda va a un tunel con su mismo nombre; asi las senales llegan a donde hacen falta sin cruzar cables.
  //   2. ESCRITURA: WA (5 bits) y WE entran al decodificador, que activa la linea EN_n del registro elegido. Los otros 30 registros no reciben habilitacion y conservan su valor.
  //   3. REGISTROS: cada R1..R31 es un registro de 32 bits. Su entrada D recibe WD, su reloj es CLK y su borrado es RESET. Guarda WD solo en el flanco de subida de CLK y solo si su EN vale 1.
  //   4. LECTURA: dos multiplexores de 32 entradas eligen el registro n segun RA1 y RA2. Son combinacionales: RD1 y RD2 cambian en cuanto cambian RA1 y RA2, sin esperar al reloj.
  //      Por eso una instruccion puede leer dos registros y, en el mismo ciclo, escribir un tercero: la lectura es inmediata y la escritura ocurre al final, en el flanco.
  //   5. $zero: la entrada 0 de los multiplexores es una constante 0, y la salida 0 del decodificador no se conecta. El registro 0 siempre vale 0 y no se puede escribir.
  //   6. RESET: pone todos los registros a 0 al instante (borrado asincrono, no espera al reloj). Mientras RESET = 1 no se puede escribir.
  //   7. $gp y $sp: tras el reset deben valer 0x1800 y 0x3FFC, pero el componente registro solo se borra a 0. Por eso estos dos guardan el valor combinado con XOR con su valor inicial K.
  //      Escribir: se guarda WD XOR K. Leer: se calcula (valor guardado) XOR K. Como X XOR K XOR K = X, desde fuera se comporta como un registro normal, y tras RESET se lee 0 XOR K = K.
  //   8. POR QUE ASI: usar registros (no RAM) cumple la guia, y conectar todos directamente a CLK evita relojes derivados. El decodificador con WE evita escribir dos registros a la vez.
  //   Mux de lectura 1 (RA1 -> RD1)
  //   Mux de lectura 2 (RA2 -> RD2)
  //   Elige UNA de las 32 entradas R_n
  //   segun RA1 y la copia en RD1.
  //   Es combinacional: no usa reloj.
  //   Elige UNA de las 32 entradas R_n
  //   segun RA2 y la copia en RD2.
  //   Es combinacional: no usa reloj.
endmodule

module ALU (
  input  [31:0] A,
  input  [31:0] B,
  input  [2:0] OP,
  output [31:0] RESULT,
  output ZERO
);

  wire LT, SUB;
  wire [31:0] ANDR, BB, NB, ORR, SLLR, SLTR, SRLR, SUM;

  Comparator #(.mode("unsigned"), .width(3)) comparator_1 (.a(OP), .b(3'b001), .eq(SUB));  // open: gt, lt
  assign NB = ~B;  // NOT_Gate not_1, 32 bits wide
  Multiplexer #(.width(32)) multiplexer_1 (.in0(B), .in1(NB), .out(BB), .sel(SUB));
  Adder #(.width(32)) adder_1 (.a(A), .b(BB), .out(SUM), .cin(SUB));  // open: cout
  assign ANDR = A & B;  // AND_Gate and_1, 32 bits wide
  assign ORR = A | B;  // OR_Gate or_1, 32 bits wide
  Comparator #(.width(32)) comparator_2 (.a(A), .b(B), .lt(LT));  // open: gt, eq
  assign SLTR = {{31{1'b0}}, LT};  // Bit_Extender bit_extender_1
  Shifter #(.width(32)) shifter_1 (.in(B), .\dist (A[4:0]), .out(SLLR));
  Shifter #(.shift("lr"), .width(32)) shifter_2 (.in(B), .\dist (A[4:0]), .out(SRLR));
  Multiplexer #(.select(3), .width(32)) multiplexer_2 (
    .in0(SUM), .in1(SUM), .in2(ANDR), .in3(ORR), .in4(SLTR), .in5(SLLR), .in6(SRLR), .in7({32{1'b0}}),
    .out(RESULT), .sel(OP));
  Comparator #(.width(32)) comparator_3 (.a(RESULT), .b({32{1'b0}}), .eq(ZERO));  // open: gt, lt

  // Other names for the same wires on the sheet: SHAMT[4:0] = A[4:0]; RES[31:0] = RESULT; Z = ZERO

  // Notes on the sheet:
  //   se ignoran.
  //   SENAL ZERO
  //   CODIGO OP = 111
  //   indefinido.
  //   COMO FUNCIONA LA ALU
  //   POR QUE UN SOLO SUMADOR
  //   restar es A + (B negado) + 1 (complemento a dos).
  //   POR QUE EL COMPARADOR VA CON SIGNO
  //   DESPLAZAMIENTOS (SLL y SRL)
  //   A: primer operando (32 bits)
  //   B: segundo operando (32 bits)
  //   OP: elige la operacion (3 bits)
  //   La ALU es combinacional: no guarda nada. RESULT depende solo de A, B y OP.
  //   Calcula TODAS las operaciones a la vez, cada una en su bloque (columna derecha).
  //   Al final, un multiplexor de 8 entradas elige segun OP cual resultado sale.
  //   La guia pide una unica ALU y ningun otro sumador. Suma y resta comparten uno:
  //   ADD: el multiplexor deja pasar B y el acarreo de entrada vale 0.
  //   SUB: deja pasar NB (B negado) y el acarreo de entrada vale 1 (senal SUB).
  //   Ejemplo: 5 - 7 = 5 + 0xFFFFFFF8 + 1 = 0xFFFFFFFE, que es -2.
  //   slt compara numeros con signo: 0xFFFFFFFF vale -1, que es menor que 1.
  //   Un comparador sin signo diria lo contrario; por eso va en complemento a dos.
  //   Mueven los bits de B tantas posiciones como diga A[4:0] (de 0 a 31) y rellenan
  //   con ceros. La CPU pondra en A el shamt de la instruccion. Los bits altos de A
  //   Compara RESULT con 0. Para beq/bne la CPU resta los dos registros y mira ZERO.
  //   Ninguna instruccion lo usa; sale una constante 0 para que RESULT nunca quede
  //   Codificacion de OP
  //   000  ADD   A + B
  //   001  SUB   A - B
  //   010  AND   A AND B
  //   011  OR    A OR B
  //   100  SLT   1 si A < B (con signo), si no 0
  //   101  SLL   B << A[4:0]
  //   110  SRL   B >> A[4:0] (logico)
  //   111  sin uso (resultado 0)
  //   En SLL/SRL el operando A trae la cantidad a desplazar (solo se usan sus 5 bits bajos)
  //   y B trae el valor a desplazar.
  //   ZERO: 1 si RESULT vale 0
  //   RESULT: resultado de 32 bits
  //   ALU: una sola ALU combinacional de 32 bits
  //   Entradas A, B (32 bits) y OP (3 bits). Salidas RESULT (32 bits) y ZERO (1 si RESULT = 0).
  //   SUB = 1 cuando OP = 001 (resta)
  //   NB = B negado bit a bit
  //   BB = B (suma) o NB (resta)
  //   Unico sumador: SUM = A + BB + SUB  (A - B = A + ~B + 1)
  //   ANDR = A AND B
  //   ORR = A OR B
  //   Cada bit del resultado es el OR de los bits de A y B. Solo sale si OP = 011.
  //   Comparador CON SIGNO: LT = 1 si A < B
  //   LT = 1 si A < B. Va CON SIGNO: asi -1 (0xFFFFFFFF) es menor que 1, como exige slt.
  //   SLTR = 31 ceros y LT en el bit 0
  //   SHAMT = A[4:0]: cantidad de bits a desplazar
  //   SLLR = B desplazado a la izquierda SHAMT bits (rellena con 0)
  //   SRLR = B desplazado a la derecha SHAMT bits (logico, rellena con 0)
  //   ZERO32: valor del codigo sin usar (OP = 111)
  //   RES = operacion elegida por OP (ver tabla)
  //   Z = 1 cuando RES = 0  (salida ZERO)
  //   Compara OP con 001: si es resta, SUB = 1. Esa senal elige NB y pone a 1 el acarreo del sumador.
  //   NB es B con todos los bits invertidos: es la mitad del truco para restar (A - B = A + NB + 1).
  //   Con SUB = 0 pasa B (suma). Con SUB = 1 pasa NB (resta). Asi un solo sumador sirve para las dos.
  //   Su acarreo de entrada es SUB. El acarreo de salida se descarta: el resultado es modulo 2^32.
  //   Cada bit del resultado es el AND de los bits de A y B. Se calcula siempre; solo sale si OP = 010.
  //   RESULT tiene 32 bits y LT solo 1: se rellena con 31 ceros a la izquierda. El resultado es 0 o 1.
  //   Un divisor de bits (splitter) separa los 5 bits bajos de A: la cantidad a desplazar (0 a 31).
  //   Cada posicion a la izquierda multiplica por 2. Entra B como dato y SHAMT como distancia.
  //   Cada posicion a la derecha divide por 2 sin signo: rellena con ceros, no copia el bit de signo.
  //   Es la entrada 7 del multiplexor final: evita que RESULT quede indefinido con un OP sin uso.
  //   El selector OP (000..111) elige la entrada 0..7: SUM, SUM, ANDR, ORR, SLTR, SLLR, SRLR, ZERO32.
  //   Compara RES con la constante 0. Su salida de igualdad es ZERO, que la CPU usara en beq y bne.
endmodule
